// Logisim project RAMLogic.circ as structural Verilog: 1 circuit, main circuit main
module main (
);

  wire [3:0] ram_1_data, undriven;
  wire [7:0] demultiplexer_1_out7, demultiplexer_2_out7, demultiplexer_3_out7, demultiplexer_4_out7;

  RAM #(.addrWidth(10), .dataWidth(4), .databus("bidir"), .trigger("high")) ram_1 (
    .addr({{6{1'b0}}, undriven}), .data(ram_1_data));  // open: we, oe
  Demultiplexer #(.select(3)) demultiplexer_1 (
    .out0(demultiplexer_1_out7[7]), .out1(demultiplexer_1_out7[6]), .out2(demultiplexer_1_out7[5]),
    .out3(demultiplexer_1_out7[4]), .out4(demultiplexer_1_out7[3]), .out5(demultiplexer_1_out7[2]),
    .out6(demultiplexer_1_out7[1]), .out7(demultiplexer_1_out7[0]), .in(ram_1_data[0]));  // open: sel
  Controlled_Buffer controlled_buffer_1 (.out(ram_1_data[0]));  // open: in, en
  Controlled_Buffer controlled_buffer_2 (.out(ram_1_data[1]));  // open: in, en
  Demultiplexer #(.select(3)) demultiplexer_2 (
    .out0(demultiplexer_2_out7[7]), .out1(demultiplexer_2_out7[6]), .out2(demultiplexer_2_out7[5]),
    .out3(demultiplexer_2_out7[4]), .out4(demultiplexer_2_out7[3]), .out5(demultiplexer_2_out7[2]),
    .out6(demultiplexer_2_out7[1]), .out7(demultiplexer_2_out7[0]), .in(ram_1_data[1]));  // open: sel
  Controlled_Buffer controlled_buffer_3 (.out(ram_1_data[2]));  // open: in, en
  Controlled_Buffer controlled_buffer_4 (.out(ram_1_data[3]));  // open: in, en
  Demultiplexer #(.select(3)) demultiplexer_3 (
    .out0(demultiplexer_3_out7[7]), .out1(demultiplexer_3_out7[6]), .out2(demultiplexer_3_out7[5]),
    .out3(demultiplexer_3_out7[4]), .out4(demultiplexer_3_out7[3]), .out5(demultiplexer_3_out7[2]),
    .out6(demultiplexer_3_out7[1]), .out7(demultiplexer_3_out7[0]), .in(ram_1_data[2]));  // open: sel
  DotMatrix #(.matrixcols(4), .matrixrows(8)) dotmatrix_1 (
    .col0(demultiplexer_1_out7), .col1(demultiplexer_2_out7), .col2(demultiplexer_3_out7),
    .col3(demultiplexer_4_out7));
  Demultiplexer #(.select(3)) demultiplexer_4 (
    .out0(demultiplexer_4_out7[7]), .out1(demultiplexer_4_out7[6]), .out2(demultiplexer_4_out7[5]),
    .out3(demultiplexer_4_out7[4]), .out4(demultiplexer_4_out7[3]), .out5(demultiplexer_4_out7[2]),
    .out6(demultiplexer_4_out7[1]), .out7(demultiplexer_4_out7[0]), .in(ram_1_data[3]));  // open: sel
endmodule
